// Logisim project 4bitCounter.circ as structural Verilog: 1 circuit, main circuit main
module main (
  input  CLK,
  output a,
  output b,
  output c,
  output d
);

  wire and_1_out, and_2_out, and_3_out, and_4_out, and_5_out, and_6_out, and_7_out, not_1_out, not_2_out,
       not_3_out, not_4_out, not_5_out, not_6_out, not_7_out, not_8_out, or_1_out, or_2_out, or_3_out;

  and and_1 (and_1_out, b, c, d);
  and and_2 (and_2_out, a, not_1_out);
  not not_1 (not_1_out, d);
  not not_2 (not_2_out, c);
  and and_3 (and_3_out, not_2_out, b);
  and and_4 (and_4_out, d, c, not_3_out);
  not not_3 (not_3_out, b);
  and and_5 (and_5_out, b, not_4_out);
  not not_4 (not_4_out, d);
  not not_5 (not_5_out, a);
  and and_6 (and_6_out, not_5_out, not_6_out, d);
  not not_6 (not_6_out, c);
  and and_7 (and_7_out, c, not_7_out);
  not not_7 (not_7_out, d);
  not not_8 (not_8_out, d);
  or or_1 (or_1_out, and_1_out, and_2_out);
  or or_2 (or_2_out, and_3_out, and_4_out, and_5_out);
  or or_3 (or_3_out, and_6_out, and_7_out);
  Register #(.width(1)) a_prime (.D(or_1_out), .Q(a), .clk(CLK));  // open: en, clr
  Register #(.width(1)) b_prime (.D(or_2_out), .Q(b), .clk(CLK));  // open: en, clr
  Register #(.width(1)) c_prime (.D(or_3_out), .Q(c), .clk(CLK));  // open: en, clr
  Register #(.width(1)) d_prime (.D(not_8_out), .Q(d), .clk(CLK));  // open: en, clr

  // Notes on the sheet:
  //   b
  //   a
  //   c
  //   d
endmodule
