// Logisim project counter.circ as structural Verilog: 3 circuits, main circuit main
module main (
);

  wire bcd_decoder_1_a_2, bcd_decoder_1_b, bcd_decoder_1_c, bcd_decoder_1_d, bcd_decoder_1_e,
       bcd_decoder_1_f, bcd_decoder_1_g, Clock_out, counter_a, counter_b, counter_c, counter_d;

  Clock Clock (.out(Clock_out));
  _4BitCounter counter (.CLK(Clock_out), .a(counter_a), .b(counter_b), .c(counter_c), .d(counter_d));
  BCD_decoder bcd_decoder_1 (
    .a(counter_a), .in_2(counter_b), .in_3(counter_c), .in_4(counter_d), .a_2(bcd_decoder_1_a_2),
    .b(bcd_decoder_1_b), .c(bcd_decoder_1_c), .d(bcd_decoder_1_d), .e(bcd_decoder_1_e), .f(bcd_decoder_1_f),
    .g(bcd_decoder_1_g));
  _7_Segment_Display u_7_segment_display_1 (
    .g(bcd_decoder_1_g), .f(bcd_decoder_1_f), .a(bcd_decoder_1_a_2), .b(bcd_decoder_1_b),
    .e(bcd_decoder_1_e), .d(bcd_decoder_1_d), .c(bcd_decoder_1_c));  // open: dp
endmodule

module _4BitCounter (
  input  CLK,
  output a,
  output b,
  output c,
  output d
);

  wire and_1_out, and_2_out, and_3_out, and_4_out, and_5_out, and_6_out, and_7_out, not_1_out, not_2_out,
       not_3_out, not_4_out, not_5_out, not_6_out, not_7_out, not_8_out, or_1_out, or_2_out, or_3_out;

  and and_1 (and_1_out, b, c, d);
  and and_2 (and_2_out, a, not_1_out);
  not not_1 (not_1_out, d);
  not not_2 (not_2_out, c);
  and and_3 (and_3_out, not_2_out, b);
  and and_4 (and_4_out, d, c, not_3_out);
  not not_3 (not_3_out, b);
  and and_5 (and_5_out, b, not_4_out);
  not not_4 (not_4_out, d);
  not not_5 (not_5_out, a);
  and and_6 (and_6_out, not_5_out, not_6_out, d);
  not not_6 (not_6_out, c);
  and and_7 (and_7_out, c, not_7_out);
  not not_7 (not_7_out, d);
  not not_8 (not_8_out, d);
  or or_1 (or_1_out, and_1_out, and_2_out);
  or or_2 (or_2_out, and_3_out, and_4_out, and_5_out);
  or or_3 (or_3_out, and_6_out, and_7_out);
  Register #(.width(1)) a_prime (.D(or_1_out), .Q(a), .clk(CLK));  // open: en, clr
  Register #(.width(1)) b_prime (.D(or_2_out), .Q(b), .clk(CLK));  // open: en, clr
  Register #(.width(1)) c_prime (.D(or_3_out), .Q(c), .clk(CLK));  // open: en, clr
  Register #(.width(1)) d_prime (.D(not_8_out), .Q(d), .clk(CLK));  // open: en, clr

  // Notes on the sheet:
  //   b
  //   a
  //   c
  //   d
endmodule

module BCD_decoder (
  input  a,
  input  in_2,
  input  in_3,
  input  in_4,
  output a_2,
  output b,
  output c,
  output d,
  output e,
  output f,
  output g
);

  wire and_1_out, and_2_out, and_3_out, and_4_out, and_5_out, and_6_out, and_7_out, and_8_out, and_9_out,
       and_10_out, not_1_out, not_2_out, not_3_out, not_4_out, not_5_out, not_6_out, not_7_out, not_8_out,
       not_9_out, not_10_out, not_11_out, not_12_out, not_13_out, not_14_out, not_15_out, xnor_1_out,
       xnor_2_out, xor_1_out;

  not not_1 (not_1_out, in_4);
  not not_2 (not_2_out, in_2);
  not not_3 (not_3_out, in_4);
  not not_4 (not_4_out, in_2);
  not not_5 (not_5_out, in_3);
  not not_6 (not_6_out, in_4);
  not not_7 (not_7_out, in_2);
  not not_8 (not_8_out, in_4);
  not not_9 (not_9_out, in_3);
  not not_10 (not_10_out, in_4);
  not not_11 (not_11_out, in_3);
  not not_12 (not_12_out, in_4);
  not not_13 (not_13_out, in_4);
  xnor xnor_1 (xnor_1_out, in_2, in_4);
  not not_14 (not_14_out, in_2);
  xnor xnor_2 (xnor_2_out, in_3, in_4);
  not not_15 (not_15_out, in_3);
  and and_1 (and_1_out, in_3, not_1_out);
  and and_2 (and_2_out, not_2_out, in_3);
  and and_3 (and_3_out, not_3_out, not_4_out);
  and and_4 (and_4_out, in_2, not_5_out, in_4);
  and and_5 (and_5_out, in_3, not_6_out);
  and and_6 (and_6_out, not_7_out, not_8_out);
  and and_7 (and_7_out, not_9_out, not_10_out);
  and and_8 (and_8_out, in_2, not_11_out);
  and and_9 (and_9_out, in_2, not_12_out);
  and and_10 (and_10_out, in_3, not_13_out);
  xor xor_1 (xor_1_out, in_2, in_3);
  or or_1 (a_2, a, in_3, xnor_1_out);
  or or_2 (b, not_14_out, xnor_2_out);
  or or_3 (c, not_15_out, in_4, in_2);
  or or_4 (d, a, and_1_out, and_2_out, and_3_out, and_4_out);
  or or_5 (e, and_5_out, and_6_out);
  or or_6 (f, a, and_7_out, and_8_out, and_9_out);
  or or_7 (g, a, and_10_out, xor_1_out);

  // Notes on the sheet:
  //   b
  //   c
  //   d
endmodule
