// Logisim project sevenSegDisplay.circ as structural Verilog: 1 circuit, main circuit main
module main (
);

  wire undriven, undriven_2, undriven_3, undriven_4, undriven_5, undriven_6, undriven_7;

  _7_Segment_Display u_7_segment_display_1 (
    .g(undriven), .f(undriven_3), .a(undriven_5), .b(undriven_7), .e(undriven_2), .d(undriven_4),
    .c(undriven_6), .dp(1'b0));
endmodule
